# Fritzing sketch Vu_pcb2 (saved by Fritzing 0.9.3b)
circuit board: 5.04815cm x 5.99464cm
breadboards: 1

parts:
  C1 = Electrolytic Capacitor [capacitance=10µF package="100 mil [THT, electrolytic]"]
  C2 = Electrolytic Capacitor [capacitance=10µF package="100 mil [THT, electrolytic]"]
  R1 = Resistor [tolerance=±5% resistance=100k package=THT]
  R2 = Resistor [tolerance=±5% resistance=100k package=THT]
  R3 = Resistor [tolerance=±5% resistance=100k package=THT]
  R4 = Resistor [tolerance=±5% resistance=100k package=THT]
  R5 = Resistor [tolerance=±5% resistance=330 package=THT]
  NANO = Arduino Nano (Rev3.0)
  R7 = Resistor [tolerance=±5% resistance=10k package=THT]
  R6 = Resistor [tolerance=±5% resistance=330 package=THT]
  AUX_IN = 3.5mm Audio Jack [package=audio-jack]
  AUX_OUT = 3.5mm Audio Jack [package=audio-jack]
  MH-MINI-360 = Mini-360 DC-DC Buck converter [package=THT]
  C3 = Electrolytic Capacitor [capacitance=1mF package="200 mil [THT, electrolytic]"]
  C4 = Electrolytic Capacitor [capacitance=1mF package="200 mil [THT, electrolytic]"]
  C5 = Electrolytic Capacitor [capacitance=0.1mF package="100 mil [THT, electrolytic]"]
  12V = KF301-2 [form="♀ (female)" package=THT]
  MODE = KF301-2 [form="♀ (female)" package=THT]
  L_LED = KF301-3P [form="♀ (female)" package=THT]
  R_LED = KF301-3P [form="♀ (female)" package=THT]

nets:
  N1: C1.-, AUX_IN.RIGHT, AUX_OUT.RIGHT
  N2: C1.+, R3.Pin_0, R4.Pin_1, NANO.A4
  N3: C2.-, AUX_IN.LEFT, AUX_OUT.LEFT
  N4: C2.+, R1.Pin_0, R2.Pin_1, NANO.A5
  5V: R1.Pin_1, R3.Pin_1, NANO.5V, MH-MINI-360.OUT+, C3.+, C4.+, MODE.pin1, L_LED.pin2, R_LED.pin2
  GND: R2.Pin_0, R4.Pin_0, NANO.GND, R7.Pin_1, AUX_IN.SLEEVE, AUX_OUT.SLEEVE, MH-MINI-360.OUT-, C3.-, C4.-, L_LED.pin3, R_LED.pin1
  N5: R5.Pin_0, NANO.D6
  N6: R5.Pin_1, L_LED.pin1
  N7: NANO.D3, R7.Pin_0, MODE.pin2
  N8: NANO.D5, R6.Pin_0
  N9: R6.Pin_1, R_LED.pin3
  N10: MH-MINI-360.IN-, C5.-, 12V.pin1
  N11: MH-MINI-360.IN+, C5.+, 12V.pin2

notes:
  M3
  SIG +5V  GND
  GND +5V  SIG
  ARDUINO
  V3.0
  VU Lights rev 1.1
  +
  -

custom parts:
  Mini-360 DC-DC Buck converter: Mini-360 DC-DC Buck converter. Tiny buck step down voltage converter, input voltage 4.75 to 23V output 1 to 17V adjustable. Available from ebay and the like.
  KF301-2: Screw terminal
  KF301-3P: Screw terminal
